# Fritzing sketch Four Buttons and Encoder (saved by Fritzing 0.9.3b)
breadboards: 1

parts:
  PB1 = Round Pushbutton
  PB2 = Round Pushbutton
  PB3 = Round Pushbutton
  PB4 = Round Pushbutton
  PB5 = Round Pushbutton
  PB6 = Round Pushbutton
  PB7 = Round Pushbutton
  PB8 = Round Pushbutton
  PB9 = Round Pushbutton
  PB10 = Round Pushbutton
  PB11 = Round Pushbutton
  PB12 = Round Pushbutton
  TM1 = ToggleSW_Blue1
  TM2 = ToggleSW_Blue1
  TM3 = ToggleSW_Blue1
  EC1 = Rotary Encoder with switch (KY-040) [part_number=KY-040]  # not connected
  EC2 = Rotary Encoder with switch (KY-040) [part_number=KY-040]  # not connected
  EC3 = Rotary Encoder with switch (KY-040) [part_number=KY-040]  # not connected
  D1 = Diode [package=diode-1n4001]
  D2 = Diode [package=diode-1n4001]
  D3 = Diode [package=diode-1n4001]
  D4 = Diode [package=diode-1n4001]
  D5 = Diode [package=diode-1n4001]
  D6 = Diode [package=diode-1n4001]
  D7 = Diode [package=diode-1n4001]
  D8 = Diode [package=diode-1n4001]
  D9 = Diode [package=diode-1n4001]
  D10 = Diode [package=diode-1n4001]
  D11 = Diode [package=diode-1n4001]
  D12 = Diode [package=diode-1n4001]
  D13 = Diode [package=diode-1n4001]
  D14 = Diode [package=diode-1n4001]
  D15 = Diode [package=diode-1n4001]
  D16 = Diode [package=diode-1n4001]
  D17 = Diode [package=diode-1n4001]
  D18 = Diode [package=diode-1n4001]
  TG1 = Round Pushbutton
  TG2 = Round Pushbutton
  TG3 = Round Pushbutton
  TG4 = Round Pushbutton
  TG5 = Round Pushbutton
  TG6 = Round Pushbutton
  D19 = Diode [package=diode-1n4001]
  D20 = Diode [package=diode-1n4001]
  D21 = Diode [package=diode-1n4001]
  D22 = Diode [package=diode-1n4001]
  D23 = Diode [package=diode-1n4001]
  D24 = Diode [package=diode-1n4001]
  D25 = Diode [package=diode-1n4001]  # not connected
  D27 = Diode [package=diode-1n4001]  # not connected
  D28 = Diode [package=diode-1n4001]  # not connected
  D30 = Diode [package=diode-1n4001]  # not connected
  OO1 = Round Pushbutton
  D31 = Diode [package=diode-1n4001]
  OO2 = Round Pushbutton
  D32 = Diode [package=diode-1n4001]

nets:
  N1: PB1.leg0, D1.C
  N2: PB2.leg0, D2.C
  N3: PB3.leg0, D3.C
  N4: PB4.leg0, D4.C
  N5: PB5.leg0, D5.C
  N6: PB6.leg0, D6.C
  N7: PB7.leg0, D7.C
  N8: PB8.leg0, D8.C
  N9: PB9.leg0, D9.C
  N10: PB10.leg0, D10.C
  N11: PB11.leg0, D11.C
  N12: PB12.leg0, D12.C
  N13: TM1.pin_1, D23.C
  N14: TM1.pin_2, D20.C
  N15: TM2.pin_1, D24.C
  N16: TM2.pin_2, D22.C
  N17: TM3.pin_1, D19.C
  N18: TM3.pin_2, D21.C
  N19: D13.C, TG3.leg0
  N20: D14.C, TG1.leg0
  N21: D15.C, TG6.leg0
  N22: D16.C, TG4.leg0
  N23: D17.C, TG2.leg0
  N24: D18.C, TG5.leg0
  N25: OO1.leg0, D31.C
  N26: OO2.leg0, D32.C

custom parts:
  ToggleSW_Blue1: Generic Tiggle Switch on-off-on
  Rotary Encoder with switch (KY-040): A Rotary Encoder with switch
